# Fritzing sketch wt_camera_fritz_v3 (saved by Fritzing 0.9.6b)
circuit board: 4.60204cm x 3.7567cm
breadboards: 1

parts:
  S3 = Pushbutton [package="[THT]"]
  + = Camdenboss CTB0158-2 [part_number=CTB0158-2 package=THT]
  mems = male pin header, 3 pins [form="♂ (male)"]
  gnd = male pin header, 3 pins [form="♂ (male)"]
  breakout = male pin header, 7 pins [form="♂ (male)"]
  xiao = male pin header, 7 pins [form="♂ (male)"]
  10k_ohm = Pushbutton [package=THT]
  xiao_2 = male pin header, 7 pins [form="♂ (male)"]
  J = male pin header, 3 pins [form="♂ (male)"]
  3_3V = male pin header, 3 pins [form="♂ (male)"]

nets:
  N1: S3.Pin_1, mems.pin2, breakout.pin5, xiao_2.pin5, 3_3V.pin1, 3_3V.pin2, 3_3V.pin3
  N2: S3.Pin_3, xiao.pin3, 10k_ohm.leg0
  N3: +.pin1, mems.pin1, gnd.pin1, gnd.pin2, gnd.pin3, breakout.pin6, 10k_ohm.leg1, xiao_2.pin6, J.pin1
  N4: +.pin2, breakout.pin7, xiao_2.pin7
  N5: mems.pin3, xiao.pin6
  N6: breakout.pin1, xiao_2.pin1
  N7: breakout.pin2, xiao_2.pin2
  N8: breakout.pin3, xiao_2.pin3
  N9: breakout.pin4, xiao_2.pin4
  N10: xiao.pin4, J.pin2
  N11: xiao.pin5, J.pin3
